// Logisim project Full_Adder.circ as structural Verilog: 1 circuit, main circuit main
module main (
  input  a,
  input  b,
  input  c_in,
  output sum,
  output cout
);

  wire and_1_out, and_2_out, xor_1_out;

  xor xor_1 (xor_1_out, a, b);
  xor xor_2 (sum, xor_1_out, c_in);
  and and_1 (and_1_out, c_in, xor_1_out);
  and and_2 (and_2_out, b, a);
  or or_1 (cout, and_1_out, and_2_out);

  // Notes on the sheet:
  //   Full Adder
endmodule
